// Logisim project Practica05.circ as structural Verilog
// AFD
module automata (
  input  In
);

  wire clock_1_out, E1_qn, E2_qn, not_1_out, R1_out, S1_out, S2_out;
  wire [1:0] E2_q;

  Clock clock_1 (.out(clock_1_out));
  not not_1 (not_1_out, In);
  S_R_Flip_Flop E1 (.S(S1_out), .clk(clock_1_out), .R(R1_out), .Q(E2_q[1]), .Qn(E1_qn));  // open: preset, reset, en
  S_R_Flip_Flop E2 (.S(S2_out), .clk(clock_1_out), .R(E2_q[0]), .Q(E2_q[0]), .Qn(E2_qn));  // open: preset, reset, en
  and S1 (S1_out, E1_qn, E2_q[0], not_1_out);
  and R1 (R1_out, E2_q[1], E2_q[0], not_1_out);
  and S2 (S2_out, E2_qn, not_1_out);
  Hex_Digit_Display hex_digit_display_1 (.value({2'b00, E2_q}));  // open: dp

  // Notes on the sheet:
  //   Entrada del autómata
  //   0 = error
  //   1 = acierto
  //   Autómata del ejercicio 1
  //   R2
  //   Estado actual del autómata.
  //   0 = T
  //   1 = TE
  //   2 = NT
  //   3 = NTE
endmodule

// REG
module registro (
  input  Escribir,
  input  [7:0] Dato_a_escribir,
  output [7:0] \Dato_leído 
);

  D_Flip_Flop d_ff_1 (.clk(Escribir), .D(Dato_a_escribir[0]), .Q(\Dato_leído [0]));  // open: Qn, preset, en, reset
  D_Flip_Flop d_ff_2 (.clk(Escribir), .D(Dato_a_escribir[1]), .Q(\Dato_leído [1]));  // open: Qn, preset, en, reset
  D_Flip_Flop d_ff_3 (.clk(Escribir), .D(Dato_a_escribir[2]), .Q(\Dato_leído [2]));  // open: Qn, preset, en, reset
  D_Flip_Flop d_ff_4 (.clk(Escribir), .D(Dato_a_escribir[3]), .Q(\Dato_leído [3]));  // open: Qn, preset, en, reset
  D_Flip_Flop d_ff_5 (.clk(Escribir), .D(Dato_a_escribir[4]), .Q(\Dato_leído [4]));  // open: Qn, preset, en, reset
  D_Flip_Flop d_ff_6 (.clk(Escribir), .D(Dato_a_escribir[5]), .Q(\Dato_leído [5]));  // open: Qn, preset, en, reset
  D_Flip_Flop d_ff_7 (.clk(Escribir), .D(Dato_a_escribir[6]), .Q(\Dato_leído [6]));  // open: Qn, preset, en, reset
  D_Flip_Flop d_ff_8 (.clk(Escribir), .D(Dato_a_escribir[7]), .Q(\Dato_leído [7]));  // open: Qn, preset, en, reset

  // Notes on the sheet:
  //   Registro de 8 bits usando flip-flop's D
endmodule

// BANCO
module banco (
  input  [1:0] Leer_R1,
  input  [1:0] Escribir_R,
  input  [7:0] Escribir_D,
  input  [1:0] Leer_R2,
  input  Escribir,
  output [7:0] Leer_D1,
  output [7:0] Leer_D2
);

  wire demultiplexer_2_out0, demultiplexer_2_out1, demultiplexer_2_out2, demultiplexer_2_out3;
  wire [7:0] demultiplexer_1_out0, demultiplexer_1_out1, demultiplexer_1_out2, demultiplexer_1_out3,
       \registro_1_dato_leído , \registro_2_dato_leído , \registro_3_dato_leído , \registro_4_dato_leído ;

  Demultiplexer #(.select(2), .width(8), .enable("false")) demultiplexer_1 (
    .out0(demultiplexer_1_out0), .out1(demultiplexer_1_out1), .out2(demultiplexer_1_out2),
    .out3(demultiplexer_1_out3), .in(Escribir_D), .sel(Escribir_R));
  Demultiplexer #(.select(2), .enable("false")) demultiplexer_2 (
    .out0(demultiplexer_2_out0), .out1(demultiplexer_2_out1), .out2(demultiplexer_2_out2),
    .out3(demultiplexer_2_out3), .in(Escribir), .sel(Escribir_R));
  registro registro_1 (
    .Escribir(demultiplexer_2_out0), .Dato_a_escribir(demultiplexer_1_out0),
    .\Dato_leído (\registro_1_dato_leído ));
  registro registro_2 (
    .Escribir(demultiplexer_2_out1), .Dato_a_escribir(demultiplexer_1_out1),
    .\Dato_leído (\registro_2_dato_leído ));
  registro registro_3 (
    .Escribir(demultiplexer_2_out2), .Dato_a_escribir(demultiplexer_1_out2),
    .\Dato_leído (\registro_3_dato_leído ));
  registro registro_4 (
    .Escribir(demultiplexer_2_out3), .Dato_a_escribir(demultiplexer_1_out3),
    .\Dato_leído (\registro_4_dato_leído ));
  Multiplexer #(.select(2), .width(8), .enable("false")) multiplexer_1 (
    .in0(\registro_1_dato_leído ), .in1(\registro_2_dato_leído ), .in2(\registro_3_dato_leído ),
    .in3(\registro_4_dato_leído ), .out(Leer_D1), .sel(Leer_R1));
  Multiplexer #(.select(2), .width(8), .enable("false")) multiplexer_2 (
    .in0(\registro_1_dato_leído ), .in1(\registro_2_dato_leído ), .in2(\registro_3_dato_leído ),
    .in3(\registro_4_dato_leído ), .out(Leer_D2), .sel(Leer_R2));

  // Notes on the sheet:
  //   Banco de 4 registros de 8 bits
endmodule

module \interconexión  (
  input  [15:0] In,
  output out_2
);

  wire [7:0] alu_8_bits_1_a_op_b, banco_1_leer_d1, banco_1_leer_d2, multiplexer_1_out;

  banco banco_1 (
    .Escribir_D(alu_8_bits_1_a_op_b), .Escribir(In[15]), .Escribir_R(In[13:12]), .Leer_R1(In[11:10]),
    .Leer_R2(In[9:8]), .Leer_D1(banco_1_leer_d1), .Leer_D2(banco_1_leer_d2));
  Multiplexer #(.width(8), .enable("false")) multiplexer_1 (
    .in0(In[7:0]), .in1(banco_1_leer_d2), .out(multiplexer_1_out), .sel(In[14]));
  ALU_8_bits alu_8_bits_1 (
    .A(banco_1_leer_d1), .B(multiplexer_1_out), .A_op_B(alu_8_bits_1_a_op_b), .C0(1'b0), .e(1'b1),
    .Desbordamiento(out_2));  // open: Op

  // Notes on the sheet:
  //   Intercinexión entre el banco de registros y el sumador
endmodule

module XOR (
  input  P,
  input  Q,
  output P_XOR_Q
);

  wire and_1_out, and_2_out, not_1_out, not_2_out;

  not not_1 (not_1_out, P);
  not not_2 (not_2_out, Q);
  and and_1 (and_1_out, not_1_out, Q);
  and and_2 (and_2_out, P, not_2_out);
  or or_1 (P_XOR_Q, and_1_out, and_2_out);

  // Notes on the sheet:
  //   Compuerta XOR
endmodule

module ALU_1_bit (
  input  Ci,
  input  [1:0] Op,
  input  e,
  input  A,
  input  B,
  output S,
  output Ci_1
);

  wire and_1_out, and_2_out, and_3_out, not_1_out, or_1_out, or_2_out, xor_1_p_xor_q, xor_2_p_xor_q;

  and and_1 (and_1_out, B, A);
  and and_2 (and_2_out, A, B);
  or or_1 (or_1_out, A, B);
  XOR xor_1 (.P(A), .Q(B), .P_XOR_Q(xor_1_p_xor_q));
  and and_3 (and_3_out, Ci, xor_1_p_xor_q);
  or or_2 (or_2_out, and_1_out, and_3_out);
  not not_1 (not_1_out, Op[0]);
  and and_4 (Ci_1, or_2_out, not_1_out, Op[1]);
  XOR xor_2 (.P(Ci), .Q(xor_1_p_xor_q), .P_XOR_Q(xor_2_p_xor_q));
  Multiplexer #(.select(2)) multiplexer_1 (
    .in0(and_2_out), .in1(or_1_out), .in2(xor_2_p_xor_q), .out(S), .sel(Op), .en(e));  // open: in3

  // Notes on the sheet:
  //   ALU de 1 bit
endmodule

// ALU
module ALU_8_bits (
  input  [1:0] Op,
  input  C0,
  input  e,
  input  [7:0] A,
  input  [7:0] B,
  output [7:0] A_op_B,
  output Desbordamiento
);

  wire alu_1_bit_1_ci_1, alu_1_bit_2_ci_1, alu_1_bit_3_ci_1, alu_1_bit_4_ci_1, alu_1_bit_5_ci_1,
       alu_1_bit_6_ci_1, alu_1_bit_7_ci_1;

  ALU_1_bit alu_1_bit_1 (.A(A[0]), .B(B[0]), .Ci(C0), .Op(Op), .Ci_1(alu_1_bit_1_ci_1), .e(e), .S(A_op_B[0]));
  ALU_1_bit alu_1_bit_2 (
    .A(A[1]), .B(B[1]), .Ci(alu_1_bit_1_ci_1), .Op(Op), .Ci_1(alu_1_bit_2_ci_1), .e(e), .S(A_op_B[1]));
  ALU_1_bit alu_1_bit_3 (
    .A(A[2]), .B(B[2]), .Ci(alu_1_bit_2_ci_1), .Op(Op), .Ci_1(alu_1_bit_3_ci_1), .e(e), .S(A_op_B[2]));
  ALU_1_bit alu_1_bit_4 (
    .A(A[3]), .B(B[3]), .Ci(alu_1_bit_3_ci_1), .Op(Op), .Ci_1(alu_1_bit_4_ci_1), .e(e), .S(A_op_B[3]));
  ALU_1_bit alu_1_bit_5 (
    .A(A[4]), .B(B[4]), .Ci(alu_1_bit_4_ci_1), .Op(Op), .Ci_1(alu_1_bit_5_ci_1), .e(e), .S(A_op_B[4]));
  ALU_1_bit alu_1_bit_6 (
    .A(A[5]), .B(B[5]), .Ci(alu_1_bit_5_ci_1), .Op(Op), .Ci_1(alu_1_bit_6_ci_1), .e(e), .S(A_op_B[5]));
  ALU_1_bit alu_1_bit_7 (
    .A(A[6]), .B(B[6]), .Ci(alu_1_bit_6_ci_1), .Op(Op), .Ci_1(alu_1_bit_7_ci_1), .e(e), .S(A_op_B[6]));
  ALU_1_bit alu_1_bit_8 (
    .A(A[7]), .B(B[7]), .Ci(alu_1_bit_7_ci_1), .Op(Op), .Ci_1(Desbordamiento), .e(e), .S(A_op_B[7]));

  // Notes on the sheet:
  //   ALU de 8 bits
endmodule
